# Fritzing sketch dht11 (saved by Fritzing 0.9.3b)
breadboards: 1

parts:
  A1 = ESP32 DevKitc V4
  DHT11_1 = DHT11 module

nets:
  N1: A1.Pin_14, A1.Pin_32, A1.Pin_38
  N2: A1.Pin_19, DHT11_1.DATA
  N3: A1.Pin_24, DHT11_1.VCC

notes:
  DHT11 se alimenta a 5V
  Atención cuando implementes botones o cualquier otro elemento de 3.3V

custom parts:
  ESP32 DevKitc V4: ESP32-DevKitC board with ESP32-WROOM-32 module. ESP32-DevKitC V4 is a small-sized ESP32-based development board produced by Espressif. Most of the pins on the ESP module are broken out to the pin headers on the board. The pins D0, D1, D2, D3, CMD and CLK are used internally for communication between ESP32 and SPI flash memory. They are grouped on both sides near the USB connector. Avoid using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
  DHT11 module: DHT11 black pcb module
