# Fritzing sketch ds18b_basic (saved by Fritzing 0.9.10b)
breadboards: 1

parts:
  A1 = ESP32 DevKitc V4
  DS1 = DS18B20 1-Wire Temperature Sensor Probe Cable
  R1 = Resistor [tolerance=±5% power=0.25 resistance=4.7k package=THT]

nets:
  N1: A1.Pin_1, DS1.VDD, R1.Pin_0
  N2: A1.Pin_9, DS1.shield, R1.Pin_1
  N3: A1.Pin_14, A1.Pin_32, A1.Pin_38, DS1.GND

custom parts:
  ESP32 DevKitc V4: ESP32-DevKitC board with ESP32-WROOM-32 module. ESP32-DevKitC V4 is a small-sized ESP32-based development board produced by Espressif. Most of the pins on the ESP module are broken out to the pin headers on the board. The pins D0, D1, D2, D3, CMD and CLK are used internally for communication between ESP32 and SPI flash memory. They are grouped on both sides near the USB connector. Avoid using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
