# Fritzing sketch exp_meca (saved by Fritzing 1.0.0d)
breadboards: 1

parts:
  M1 = DOIT Esp32 DevKit v1 (30 pins long, 11 pins width) [part_number=ESP32S-PIN30]
  R1 = Resistor [tolerance=±5% power=0.25W resistance=330 package=THT]
  LED1 = LED - 5mm [color="Red (633nm)" current=0.030A package="5 mm [THT]"]
  LED2 = LED - 5mm [color="Orange (620nm)" current=0.030A package="5 mm [THT]"]
  LED3 = LED - 5mm [color="Blue (470nm)" current=0.030A package="5 mm [THT]"]
  LED4 = LED - 5mm [color="Green (565nm)" current=0.030A package="5 mm [THT]"]
  LED5 = LED - 5mm [color="Yellow (595nm)" current=0.030A package="5 mm [THT]"]
  R2 = Resistor [tolerance=±5% power=0.25W resistance=330 package=THT]
  R3 = Resistor [tolerance=±5% power=0.25W resistance=330 package=THT]
  R4 = Resistor [tolerance=±5% power=0.25W resistance=330 package=THT]
  R5 = Resistor [tolerance=±5% power=0.25W resistance=330 package=THT]
  S1 = Pushbutton [package="[THT]"]
  S2 = Pushbutton [package="[THT]"]
  R6 = Resistor [tolerance=±5% power=0.25W resistance=1000 package=THT]
  R7 = Resistor [tolerance=±5% power=0.25W resistance=1000 package=THT]
  J1 = Piezo Speaker

nets:
  N1: M1.3V3, R6.Pin_0, R7.Pin_0
  N2: M1.GND, M1.D34, M1.D35, R1.Pin_1, R2.Pin_1, R3.Pin_1, R4.Pin_1, R5.Pin_1, S1.Pin_3, S1.Pin_4, S2.Pin_3, S2.Pin_4, J1.pin1
  N3: M1.D32, LED1.anode
  N4: M1.D33, LED2.anode
  N5: M1.D25, LED3.anode
  N6: M1.D26, LED4.anode
  N7: M1.D27, LED5.anode
  N8: M1.D14, J1.pin2
  N9: R1.Pin_0, LED1.cathode
  N10: LED2.cathode, R2.Pin_0
  N11: LED3.cathode, R3.Pin_0
  N12: LED4.cathode, R4.Pin_0
  N13: LED5.cathode, R5.Pin_0
  N14: S1.Pin_1, S1.Pin_2, R7.Pin_1
  N15: S2.Pin_1, S2.Pin_2, R6.Pin_1

custom parts:
  DOIT Esp32 DevKit v1 (30 pins long, 11 pins width): The DOIT Esp32 DevKit v1 is one of the development board created by DOIT to evaluate the ESP-WROOM-32 module. It is based on the ESP32 microcontroller that boasts Wifi, Bluetooth, Ethernet and Low Power support all in a single chip. (vanepp) made breadboard work, adjusted pin numbering and labels and reduced size of schematic and cleaned up pcb. This chip is 30pins long (2 x15) and 11 pins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
