# Fritzing sketch input (saved by Fritzing 0.9.3b)
breadboards: 1

parts:
  A1 = ESP32 DevKitc V4
  R1 = Resistor [tolerance=±5% resistance=1k package=THT]
  S1 = Pushbutton [package="[THT]"]
  R2 = Resistor [tolerance=±5% resistance=330 package=THT]
  LED1 = LED - 5mm [color="Red (633nm)" package="5 mm [THT]"]

nets:
  N1: A1.Pin_1, S1.Pin_1, S1.Pin_2
  N2: A1.Pin_5, R1.Pin_1, S1.Pin_3, S1.Pin_4
  N3: A1.Pin_7, LED1.anode
  N4: A1.Pin_14, A1.Pin_32, A1.Pin_38, R1.Pin_0, R2.Pin_0
  N5: R2.Pin_1, LED1.cathode

custom parts:
  ESP32 DevKitc V4: ESP32-DevKitC board with ESP32-WROOM-32 module. ESP32-DevKitC V4 is a small-sized ESP32-based development board produced by Espressif. Most of the pins on the ESP module are broken out to the pin headers on the board. The pins D0, D1, D2, D3, CMD and CLK are used internally for communication between ESP32 and SPI flash memory. They are grouped on both sides near the USB connector. Avoid using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
