# Fritzing sketch keypad_basic (saved by Fritzing 0.9.10b)
breadboards: 1

parts:
  A1 = ESP32 DevKitc V4
  Keypad4x1 = Keypad Membran 4x4

nets:
  N1: A1.Pin_14, A1.Pin_32, A1.Pin_38
  N2: A1.Pin_24, Keypad4x1.Pin8
  N3: A1.Pin_25, Keypad4x1.Pin7
  N4: A1.Pin_26, Keypad4x1.Pin6
  N5: A1.Pin_27, Keypad4x1.Pin5
  N6: A1.Pin_28, Keypad4x1.Pin4
  N7: A1.Pin_29, Keypad4x1.Pin3
  N8: A1.Pin_30, Keypad4x1.Pin2
  N9: A1.Pin_31, Keypad4x1.Pin1

custom parts:
  ESP32 DevKitc V4: ESP32-DevKitC board with ESP32-WROOM-32 module. ESP32-DevKitC V4 is a small-sized ESP32-based development board produced by Espressif. Most of the pins on the ESP module are broken out to the pin headers on the board. The pins D0, D1, D2, D3, CMD and CLK are used internally for communication between ESP32 and SPI flash memory. They are grouped on both sides near the USB connector. Avoid using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
  Keypad Membran 4x4: Membrane Keypad 4x4 Matrix
