# Fritzing sketch lcd_basic (saved by Fritzing 0.9.10b)
breadboards: 1

parts:
  A1 = ESP32 DevKitc V4
  Part1 = LCD1602-I2C

nets:
  N1: A1.Pin_14, A1.Pin_32, A1.Pin_38, Part1.GND
  N2: A1.Pin_19, Part1.VCC
  N3: A1.Pin_33, Part1.SDA
  N4: A1.Pin_36, Part1.SCL

custom parts:
  ESP32 DevKitc V4: ESP32-DevKitC board with ESP32-WROOM-32 module. ESP32-DevKitC V4 is a small-sized ESP32-based development board produced by Espressif. Most of the pins on the ESP module are broken out to the pin headers on the board. The pins D0, D1, D2, D3, CMD and CLK are used internally for communication between ESP32 and SPI flash memory. They are grouped on both sides near the USB connector. Avoid using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
  LCD1602-I2C: A standard character display, usually with 2x16 characters. Comes in many colors with LCM1602 IIC attached.
