# Fritzing sketch ldr_led (saved by Fritzing 0.9.3b)
breadboards: 1

parts:
  R1 = Photocell (LDR) [package=THT]
  R2 = Resistor [tolerance=±5% resistance=10k package=THT]
  LED1 = LED - 5mm [color="Red (633nm)" package="5 mm [THT]"]
  R3 = Resistor [tolerance=±5% resistance=330 package=THT]  # not connected
  A1 = ESP32 DevKitc V4

nets:
  N1: R1.pin_0, R2.Pin_1, A1.Pin_5
  N2: R1.pin_1, A1.Pin_1
  N3: R2.Pin_0, A1.Pin_14, A1.Pin_32, A1.Pin_38
  N4: LED1.anode, A1.Pin_9

custom parts:
  ESP32 DevKitc V4: ESP32-DevKitC board with ESP32-WROOM-32 module. ESP32-DevKitC V4 is a small-sized ESP32-based development board produced by Espressif. Most of the pins on the ESP module are broken out to the pin headers on the board. The pins D0, D1, D2, D3, CMD and CLK are used internally for communication between ESP32 and SPI flash memory. They are grouped on both sides near the USB connector. Avoid using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
