# Fritzing sketch modor_dc_basic (saved by Fritzing 0.9.10b)
breadboards: 1

parts:
  L298N1 = L298N DC motor driver
  A1 = ESP32 DevKitc V4
  PSU1 = Adjustable Breadboard Power Supply
  M1 = DC Motor [voltage_(max)=6V voltage_(min)=3V]
  S1 = Pushbutton [package="[THT]"]
  S2 = Pushbutton [package="[THT]"]
  R1 = Resistor [tolerance=±5% power=0.25 resistance=1k package=THT]
  R2 = Resistor [tolerance=±5% power=0.25 resistance=1k package=THT]

nets:
  N1: L298N1.OUT1, M1.pin_2
  N2: L298N1.OUT2, M1.pin_1
  N3: L298N1.GND, A1.Pin_14, A1.Pin_32, A1.Pin_38, PSU1.Vout-, R1.Pin_0, R2.Pin_0
  N4: L298N1.5V, PSU1.Vout+
  N5: L298N1.IN1, A1.Pin_31
  N6: L298N1.IN2, A1.Pin_30
  N7: A1.Pin_1, S1.Pin_1, S1.Pin_2, S2.Pin_1, S2.Pin_2
  N8: A1.Pin_5, S2.Pin_3, S2.Pin_4, R2.Pin_1
  N9: A1.Pin_6, S1.Pin_3, S1.Pin_4, R1.Pin_1

notes:
  FUENTE EXTERNA DE 5V
  En esta línea hay 5V CUIDADO
  En esta línea hay 3.3V CUIDADO

custom parts:
  L298N DC motor driver: 2x DC motor driver with 78M05 positive voltage regulator (7..35 V) L298N: max 46 V, 2 A Set 5 V Enable jumper to enable 5 V regultor (needed for the L298N) and +5 V output at screw terminal or supply external +5 V at screw terminal Set ENA and/or ENB to +5 V to enable motor permanently or supply ENA and/or ENB with PWM signal IN1 and IN2 set rotation directory for motor A (OUT1/OUT2) IN2 and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
  ESP32 DevKitc V4: ESP32-DevKitC board with ESP32-WROOM-32 module. ESP32-DevKitC V4 is a small-sized ESP32-based development board produced by Espressif. Most of the pins on the ESP module are broken out to the pin headers on the board. The pins D0, D1, D2, D3, CMD and CLK are used internally for communication between ESP32 and SPI flash memory. They are grouped on both sides near the USB connector. Avoid using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
