# Fritzing sketch potenciometer_bar_led (saved by Fritzing 0.9.3b)
breadboards: 1

parts:
  A1 = ESP32 DevKitc V4
  U1 = POT [knob_status=50% power=0.5W package=pot_mammoth]
  LED1 = LED - 5mm [color="Red (633nm)" current=0.030 package="5 mm [THT]"]
  R1 = Resistor [tolerance=±5% power=0.25 resistance=330 package=THT]
  LED2 = LED - 5mm [color="Blue (470nm)" current=30mA package="5 mm [THT]"]
  LED3 = LED - 5mm [color="Green (570nm)" current=0.030 package="5 mm [THT]"]
  R2 = Resistor [tolerance=±5% power=0.25 resistance=330 package=THT]
  R3 = Resistor [tolerance=±5% power=0.25 resistance=330 package=THT]

nets:
  N1: A1.Pin_1, U1.E
  N2: A1.Pin_5, U1.A
  N3: A1.Pin_8, LED2.anode
  N4: A1.Pin_9, LED3.anode
  N5: A1.Pin_10, LED1.anode
  N6: A1.Pin_14, A1.Pin_32, A1.Pin_38, U1.S, R1.Pin_0, R2.Pin_0, R3.Pin_0
  N7: LED1.cathode, R1.Pin_1
  N8: LED2.cathode, R3.Pin_1
  N9: LED3.cathode, R2.Pin_1

custom parts:
  ESP32 DevKitc V4: ESP32-DevKitC board with ESP32-WROOM-32 module. ESP32-DevKitC V4 is a small-sized ESP32-based development board produced by Espressif. Most of the pins on the ESP module are broken out to the pin headers on the board. The pins D0, D1, D2, D3, CMD and CLK are used internally for communication between ESP32 and SPI flash memory. They are grouped on both sides near the USB connector. Avoid using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
