# Fritzing sketch rgb_btn (saved by Fritzing 0.9.3b)
breadboards: 1

parts:
  LED1 = RGB LED (com. cathode, rgb) [package="5 mm [THT]"]
  R2 = Resistor [tolerance=±5% resistance=330 package=THT]
  R3 = Resistor [tolerance=±5% resistance=330 package=THT]
  R4 = Resistor [tolerance=±5% resistance=330 package=THT]
  S1 = Pushbutton [package="[THT]"]
  R6 = Resistor [tolerance=±5% resistance=1k package=THT]
  S2 = Pushbutton [package="[THT]"]
  R7 = Resistor [tolerance=±5% resistance=1k package=THT]
  S3 = Pushbutton [package="[THT]"]
  R8 = Resistor [tolerance=±5% resistance=1k package=THT]
  A1 = ESP32 DevKitc V4

nets:
  N1: LED1.red_anode, R4.Pin_0
  N2: LED1.common_cathode, R6.Pin_0, R7.Pin_0, R8.Pin_0, A1.Pin_14, A1.Pin_32, A1.Pin_38
  N3: LED1.green_anode, R3.Pin_0
  N4: LED1.blue_anode, R2.Pin_0
  N5: R2.Pin_1, A1.Pin_9
  N6: R3.Pin_1, A1.Pin_10
  N7: R4.Pin_1, A1.Pin_11
  N8: S1.Pin_1, S1.Pin_2, S2.Pin_1, S2.Pin_2, S3.Pin_1, S3.Pin_2, A1.Pin_1
  N9: S1.Pin_3, S1.Pin_4, R6.Pin_1, A1.Pin_5
  N10: S2.Pin_3, S2.Pin_4, R7.Pin_1, A1.Pin_6
  N11: S3.Pin_3, S3.Pin_4, R8.Pin_1, A1.Pin_7

custom parts:
  ESP32 DevKitc V4: ESP32-DevKitC board with ESP32-WROOM-32 module. ESP32-DevKitC V4 is a small-sized ESP32-based development board produced by Espressif. Most of the pins on the ESP module are broken out to the pin headers on the board. The pins D0, D1, D2, D3, CMD and CLK are used internally for communication between ESP32 and SPI flash memory. They are grouped on both sides near the USB connector. Avoid using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
