# Fritzing sketch ultrasonic_bar (saved by Fritzing 0.9.3b)
breadboards: 1

parts:
  hc-sr1 = hc-sr04
  A1 = ESP32 DevKitc V4
  LED1 = LED - 5mm [color="Blue (525nm)" package="5 mm [THT]"]
  LED2 = LED - 5mm [color="Green (570nm)" package="5 mm [THT]"]
  LED3 = LED - 5mm [color="Yellow (595nm)" package="5 mm [THT]"]
  LED4 = LED - 5mm [color="Orange (620nm)" package="5 mm [THT]"]
  LED5 = LED - 5mm [color="Red (633nm)" package="5 mm [THT]"]
  LED6 = LED - 5mm [color="White (8000K)" package="5 mm [THT]"]
  LED7 = LED - 5mm [color="Infrared (940nm)" package="5 mm [THT]"]
  R1 = Resistor [tolerance=±5% resistance=330 package=THT]
  R2 = Resistor [tolerance=±5% resistance=330 package=THT]
  R3 = Resistor [tolerance=±5% resistance=330 package=THT]
  R4 = Resistor [tolerance=±5% resistance=330 package=THT]
  R5 = Resistor [tolerance=±5% resistance=330 package=THT]
  R6 = Resistor [tolerance=±5% resistance=330 package=THT]
  R7 = Resistor [tolerance=±5% resistance=330 package=THT]

nets:
  N1: hc-sr1.VCC, A1.Pin_19
  N2: hc-sr1.Trig, A1.Pin_26
  N3: hc-sr1.Echo, A1.Pin_24
  N4: hc-sr1.GND, A1.Pin_14, A1.Pin_32, A1.Pin_38, R1.Pin_0, R2.Pin_0, R3.Pin_0, R4.Pin_0, R5.Pin_0, R6.Pin_0, R7.Pin_0
  N5: A1.Pin_7, LED5.anode
  N6: A1.Pin_8, LED4.anode
  N7: A1.Pin_9, LED3.anode
  N8: A1.Pin_10, LED2.anode
  N9: A1.Pin_11, LED1.anode
  N10: A1.Pin_12, LED6.anode
  N11: A1.Pin_13, LED7.anode
  N12: LED1.cathode, R3.Pin_1
  N13: LED2.cathode, R4.Pin_1
  N14: LED3.cathode, R5.Pin_1
  N15: LED4.cathode, R6.Pin_1
  N16: LED5.cathode, R7.Pin_1
  N17: LED6.cathode, R2.Pin_1
  N18: LED7.cathode, R1.Pin_1

custom parts:
  ESP32 DevKitc V4: ESP32-DevKitC board with ESP32-WROOM-32 module. ESP32-DevKitC V4 is a small-sized ESP32-based development board produced by Espressif. Most of the pins on the ESP module are broken out to the pin headers on the board. The pins D0, D1, D2, D3, CMD and CLK are used internally for communication between ESP32 and SPI flash memory. They are grouped on both sides near the USB connector. Avoid using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
