# Fritzing sketch display_7segm_btn (saved by Fritzing 0.9.10b)
breadboards: 1

parts:
  A1 = ESP32 DevKitc V4
  7_Segment1 = 7 Segment Display
  R1 = Resistor [tolerance=±5% power=0.25 resistance=330 package=THT]
  R3 = Resistor [tolerance=±5% power=0.25 resistance=330 package=THT]
  R4 = Resistor [tolerance=±5% power=0.25 resistance=330 package=THT]
  R5 = Resistor [tolerance=±5% power=0.25 resistance=330 package=THT]
  R7 = Resistor [tolerance=±5% power=0.25 resistance=330 package=THT]
  R8 = Resistor [tolerance=±5% power=0.25 resistance=330 package=THT]
  R9 = Resistor [tolerance=±5% power=0.25 resistance=330 package=THT]
  S1 = Pushbutton [package="[THT]"]
  R10 = Resistor [tolerance=±5% power=0.25 resistance=1k package=THT]

nets:
  N1: A1.Pin_5, S1.Pin_1, S1.Pin_2
  N2: A1.Pin_9, R3.Pin_0
  N3: A1.Pin_10, R1.Pin_0
  N4: A1.Pin_11, R8.Pin_0
  N5: A1.Pin_12, R9.Pin_0
  N6: A1.Pin_13, R7.Pin_0
  N7: A1.Pin_14, A1.Pin_32, A1.Pin_38
  N8: A1.Pin_30, R5.Pin_0
  N9: A1.Pin_31, R4.Pin_0
  N10: 7_Segment1.Segment_E, R7.Pin_1
  N11: 7_Segment1.Segment_D, R9.Pin_1
  N12: 7_Segment1.common_cathode, R10.Pin_0
  N13: 7_Segment1.Segment_C, R8.Pin_1
  N14: 7_Segment1.Segment_B, R1.Pin_1
  N15: 7_Segment1.Segment_A, R3.Pin_1
  N16: 7_Segment1.Segment_F, R4.Pin_1
  N17: 7_Segment1.Segment_G, R5.Pin_1
  N18: S1.Pin_3, S1.Pin_4, R10.Pin_1

custom parts:
  ESP32 DevKitc V4: ESP32-DevKitC board with ESP32-WROOM-32 module. ESP32-DevKitC V4 is a small-sized ESP32-based development board produced by Espressif. Most of the pins on the ESP module are broken out to the pin headers on the board. The pins D0, D1, D2, D3, CMD and CLK are used internally for communication between ESP32 and SPI flash memory. They are grouped on both sides near the USB connector. Avoid using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
