# Fritzing sketch ldr_led_bar (saved by Fritzing 0.9.3b)
breadboards: 1

parts:
  R1 = Photocell (LDR) [package=THT]
  R2 = Resistor [tolerance=±5% resistance=10k package=THT]
  LED1 = LED - 5mm [color="Red (633nm)" package="5 mm [THT]"]
  R3 = Resistor [tolerance=±5% resistance=330 package=THT]
  A1 = ESP32 DevKitc V4
  R4 = Resistor [tolerance=±5% resistance=330 package=THT]
  LED2 = LED - 5mm [color="Orange (605nm)" package="5 mm [THT]"]
  LED3 = LED - 5mm [color="Blue (525nm)" package="5 mm [THT]"]
  LED4 = LED - 5mm [color="Green (555nm)" package="5 mm [THT]"]
  R5 = Resistor [tolerance=±5% resistance=330 package=THT]
  R6 = Resistor [tolerance=±5% resistance=330 package=THT]

nets:
  N1: R1.pin_0, R2.Pin_1, A1.Pin_5
  N2: R1.pin_1, A1.Pin_1
  N3: R2.Pin_0, R3.Pin_1, A1.Pin_14, A1.Pin_32, A1.Pin_38, R4.Pin_1, R5.Pin_1, R6.Pin_1
  N4: LED1.cathode, R3.Pin_0
  N5: LED1.anode, A1.Pin_9
  N6: A1.Pin_10, LED2.anode
  N7: A1.Pin_11, LED3.anode
  N8: A1.Pin_12, LED4.anode
  N9: R4.Pin_0, LED2.cathode
  N10: LED3.cathode, R5.Pin_0
  N11: LED4.cathode, R6.Pin_0

custom parts:
  ESP32 DevKitc V4: ESP32-DevKitC board with ESP32-WROOM-32 module. ESP32-DevKitC V4 is a small-sized ESP32-based development board produced by Espressif. Most of the pins on the ESP module are broken out to the pin headers on the board. The pins D0, D1, D2, D3, CMD and CLK are used internally for communication between ESP32 and SPI flash memory. They are grouped on both sides near the USB connector. Avoid using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
