# Fritzing sketch motor_pap (saved by Fritzing 0.9.3b)
breadboards: 1

parts:
  Driver1 = 28BYJ-48 Driver Module [part_number=ULN2003 package=THT]
  SM1 = 28BYJ-48 Stepper Motor [part_number=28BYJ-48]  # not connected
  PSU1 = Adjustable Breadboard Power Supply
  A1 = ESP32 DevKitc V4
  S3 = Pushbutton [package="[THT]"]
  S4 = Pushbutton [package="[THT]"]
  R3 = Resistor [tolerance=±5% power=0.25 resistance=1k package=THT]
  R4 = Resistor [tolerance=±5% power=0.25 resistance=1k package=THT]

nets:
  N1: Driver1.IN1, A1.Pin_9
  N2: Driver1.IN2, A1.Pin_10
  N3: Driver1.IN3, A1.Pin_11
  N4: Driver1.IN4, A1.Pin_12
  N5: Driver1.GND, Driver1.ON/OFF#7, PSU1.Vout-, A1.Pin_14, A1.Pin_32, A1.Pin_38
  N6: Driver1.Vmotor, Driver1.ON/OFF#6, PSU1.Vout+
  N7: A1.Pin_1, S3.Pin_1, S3.Pin_2, S4.Pin_1, S4.Pin_2
  N8: A1.Pin_5, S4.Pin_3, S4.Pin_4, R4.Pin_1
  N9: A1.Pin_6, S3.Pin_3, S3.Pin_4, R3.Pin_1
  N10: R3.Pin_0, R4.Pin_0

notes:
  En ésta línea hay 5V o más
  En ésta línea hay 3.3V
  Fuente externa

custom parts:
  28BYJ-48 Driver Module: ULN2003 Driver Module for the 28BYJ-48 Unipolar Stepper Motor LED A - Blue wire - Bottom coil left LED B - Pink wire - Top coil left LED C - Yellow wire - Bottom coil right LED D - Orange wire - Top coil right Common rail - red Connector pins: blue - pink - yellow - orange - red Control pins - IN1 to IN4 Power pins - GND & Vmotor (5-12V) On/Off jumper (if removed, power to motor is cut).
  28BYJ-48 Stepper Motor: Unipolar Stepper Motor 28BYJ-48 Top coil - pink & orange Bottom coil - blue & yellow Common rail - red Connector pins: blue - pink - yellow - orange - red
  ESP32 DevKitc V4: ESP32-DevKitC board with ESP32-WROOM-32 module. ESP32-DevKitC V4 is a small-sized ESP32-based development board produced by Espressif. Most of the pins on the ESP module are broken out to the pin headers on the board. The pins D0, D1, D2, D3, CMD and CLK are used internally for communication between ESP32 and SPI flash memory. They are grouped on both sides near the USB connector. Avoid using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
