# Fritzing sketch rf (saved by Fritzing 0.9.10b)
breadboards: 1

parts:
  A1 = ESP32 DevKitc V4
  YK1 = YK04 [package=THT]
  LED1 = LED - 5mm [color="Red (633nm)" current=0.030 package="5 mm [THT]"]
  R1 = Resistor [tolerance=±5% resistance=330 power=0.25 package=THT]
  LED2 = LED - 5mm [color="Yellow (585nm)" current=0.030 package="5 mm [THT]"]
  R2 = Resistor [tolerance=±5% resistance=330 power=0.25 package=THT]
  LED3 = LED - 5mm [color="Green (555nm)" current=0.030 package="5 mm [THT]"]
  R3 = Resistor [tolerance=±5% resistance=330 power=0.25 package=THT]
  LED4 = LED - 5mm [color="Orange (612nm)" current=0.030 package="5 mm [THT]"]
  R4 = Resistor [tolerance=±5% resistance=330 power=0.25 package=THT]

nets:
  N1: A1.Pin_1, YK1.5V
  N2: A1.Pin_5, YK1.D0
  N3: A1.Pin_6, YK1.D1
  N4: A1.Pin_7, YK1.D2
  N5: A1.Pin_8, YK1.D3
  N6: A1.Pin_10, LED1.anode
  N7: A1.Pin_11, LED2.anode
  N8: A1.Pin_12, LED3.anode
  N9: A1.Pin_13, LED4.anode
  N10: A1.Pin_14, A1.Pin_32, A1.Pin_38, YK1.GND, R1.Pin_0, R2.Pin_0, R3.Pin_0, R4.Pin_0
  N11: LED1.cathode, R1.Pin_1
  N12: LED2.cathode, R2.Pin_1
  N13: LED3.cathode, R3.Pin_1
  N14: LED4.cathode, R4.Pin_1

notes:
  VT D3 D2 D1 D0

custom parts:
  ESP32 DevKitc V4: ESP32-DevKitC board with ESP32-WROOM-32 module. ESP32-DevKitC V4 is a small-sized ESP32-based development board produced by Espressif. Most of the pins on the ESP module are broken out to the pin headers on the board. The pins D0, D1, D2, D3, CMD and CLK are used internally for communication between ESP32 and SPI flash memory. They are grouped on both sides near the USB connector. Avoid using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
