# Fritzing sketch rgb_pot (saved by Fritzing 0.9.3b)
breadboards: 1

parts:
  LED1 = RGB LED (com. cathode, rgb) [package="5 mm [THT]"]
  R2 = Resistor [tolerance=±5% resistance=330 package=THT]
  R3 = Resistor [tolerance=±5% resistance=330 package=THT]
  R4 = Resistor [tolerance=±5% resistance=330 package=THT]
  A1 = ESP32 DevKitc V4
  R5 = Rotary Potentiometer (Small) [maximum_resistance=100kΩ package=THT]
  R6 = Rotary Potentiometer (Small) [maximum_resistance=100kΩ package=THT]
  R7 = Rotary Potentiometer (Small) [maximum_resistance=100kΩ package=THT]

nets:
  N1: LED1.red_anode, R4.Pin_0
  N2: LED1.common_cathode, A1.Pin_14, A1.Pin_32, A1.Pin_38, R5.leg1, R6.leg1, R7.leg1
  N3: LED1.green_anode, R3.Pin_0
  N4: LED1.blue_anode, R2.Pin_0
  N5: R2.Pin_1, A1.Pin_9
  N6: R3.Pin_1, A1.Pin_10
  N7: R4.Pin_1, A1.Pin_11
  N8: A1.Pin_1, R5.leg2, R6.leg2, R7.leg2
  N9: A1.Pin_5, R7.wiper
  N10: A1.Pin_6, R6.wiper
  N11: A1.Pin_7, R5.wiper

custom parts:
  ESP32 DevKitc V4: ESP32-DevKitC board with ESP32-WROOM-32 module. ESP32-DevKitC V4 is a small-sized ESP32-based development board produced by Espressif. Most of the pins on the ESP module are broken out to the pin headers on the board. The pins D0, D1, D2, D3, CMD and CLK are used internally for communication between ESP32 and SPI flash memory. They are grouped on both sides near the USB connector. Avoid using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
