# Fritzing sketch servo_pot (saved by Fritzing 0.9.3b)
breadboards: 1

parts:
  J1 = Basic Servo
  R1 = Rotary Potentiometer (Small) [maximum_resistance=100kΩ package=THT]
  PSU1 = Adjustable Breadboard Power Supply
  A1 = ESP32 DevKitc V4

nets:
  N1: J1.gnd, PSU1.Vout-
  N2: J1.vcc, PSU1.Vout+
  N3: J1.pulse, A1.Pin_9
  N4: R1.leg1, A1.Pin_1, A1.Pin_14, A1.Pin_32, A1.Pin_38
  N5: R1.wiper, A1.Pin_5

notes:
  Fuente externa de 5V
  Voltaje de 3.3V

custom parts:
  ESP32 DevKitc V4: ESP32-DevKitC board with ESP32-WROOM-32 module. ESP32-DevKitC V4 is a small-sized ESP32-based development board produced by Espressif. Most of the pins on the ESP module are broken out to the pin headers on the board. The pins D0, D1, D2, D3, CMD and CLK are used internally for communication between ESP32 and SPI flash memory. They are grouped on both sides near the USB connector. Avoid using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
