# Fritzing sketch ultrasonic_base (saved by Fritzing 0.9.3b)
breadboards: 1

parts:
  hc-sr1 = hc-sr04
  A1 = ESP32 DevKitc V4

nets:
  N1: hc-sr1.VCC, A1.Pin_19
  N2: hc-sr1.Trig, A1.Pin_26
  N3: hc-sr1.Echo, A1.Pin_24
  N4: hc-sr1.GND, A1.Pin_14, A1.Pin_32, A1.Pin_38

custom parts:
  ESP32 DevKitc V4: ESP32-DevKitC board with ESP32-WROOM-32 module. ESP32-DevKitC V4 is a small-sized ESP32-based development board produced by Espressif. Most of the pins on the ESP module are broken out to the pin headers on the board. The pins D0, D1, D2, D3, CMD and CLK are used internally for communication between ESP32 and SPI flash memory. They are grouped on both sides near the USB connector. Avoid using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
